// Logisim project tower.circ as structural Verilog: 9 circuits, main circuit Tower
module Tower (
);

  wire AI, AO, BI, BO, CLK, clock_1_out, DVE, DVW, F_CARRY, FI, FO, HI, HLO, HLT, HO, IEND, INI, LI, LO, MI,
       MO, OPADD, OPNAND, OPNOT, OPSR, OPSUB, PCE, PCJ, PCO, RESET, RSO;
  wire [1:0] CONTROL_FLAGS;
  wire [3:0] alu_1_carry_out;
  wire [3:2] flags_1_data_out;
  wire [7:0] DATA_BUS, instructionregister_1_data_out, registers_1_a_data_out, registers_1_b_data_out;
  wire [15:0] ADDRESS_BUS;
  wire [31:27] controllogic_1_control_word;

  Clock clock_1 (.out(clock_1_out));
  and and_1 (CLK, clock_1_out, ~HLT);  // AND_Gate
  Button u_RESET (.out(RESET));
  // Probe on registers_1_a_data_out
  Registers registers_1 (
    .CLK(CLK), .RESET(RESET), .A_DATA_IN(DATA_BUS), .AI(AI), .B_DATA_IN(DATA_BUS), .BI(BI),
    .A_DATA_OUT(registers_1_a_data_out), .B_DATA_OUT(registers_1_b_data_out));
  // Probe on registers_1_b_data_out
  ProgramCounter programcounter_1 (
    .CLK(CLK), .RESET(RESET), .J(PCJ), .CO(PCO), .CE(PCE), .PC_ADDRESS_IN(ADDRESS_BUS),
    .PC_DATA_OUT(ADDRESS_BUS));
  InstructionRegister instructionregister_1 (
    .CLK(CLK), .RESET(RESET), .DATA_IN(DATA_BUS), .INI(INI), .DATA_OUT(instructionregister_1_data_out));
  ArgumentRegisters argumentregisters_1 (
    .CLK(CLK), .RESET(RESET), .DATA_IN(DATA_BUS), .HI(HI), .LI(LI), .HO(HO), .LO(LO), .HLO(HLO),
    .DATA_OUT(DATA_BUS), .ADDRESS_OUT(ADDRESS_BUS));
  assign DATA_BUS = AO ? registers_1_a_data_out : 8'bz;  // Controlled_Buffer controlled_buffer_1
  assign DATA_BUS = BO ? registers_1_b_data_out : 8'bz;  // Controlled_Buffer controlled_buffer_2
  // LedBar #(.inputtype("row")) ledbar_1: pin names not known; wires that end beside it: DATA_BUS
  // LedBar #(.inputtype("row"), .matrixcols(16)) ledbar_2: pin names not known; wires that end beside it: ADDRESS_BUS
  ControlLogic controllogic_1 (
    .CLK(CLK), .RESET(RESET), .INSTRUCTION(instructionregister_1_data_out), .FLAGS(CONTROL_FLAGS),
    .CONTROL_WORD({controllogic_1_control_word, DVW, DVE, HLO, LO, LI, HO, HI, INI, MO, MI, FO, FI, OPSR, OPNAND, OPNOT, OPSUB, OPADD, RSO, BO, BI, AO, AI, PCJ, PCO, PCE, IEND, HLT}));
  LED led_1 (.in(FO));
  LED led_2 (.in(MI));
  LED led_3 (.in(MO));
  LED led_4 (.in(INI));
  LED led_5 (.in(HI));
  LED led_6 (.in(HO));
  LED led_7 (.in(LI));
  LED led_8 (.in(LO));
  LED led_9 (.in(HLO));
  LED led_10 (.in(DVE));
  LED led_11 (.in(DVW));
  LED led_12 (.in(controllogic_1_control_word[27]));
  LED led_13 (.in(controllogic_1_control_word[28]));
  LED led_14 (.in(controllogic_1_control_word[29]));
  LED led_15 (.in(controllogic_1_control_word[30]));
  LED led_16 (.in(controllogic_1_control_word[31]));
  ALU alu_1 (
    .A_DATA_IN(registers_1_a_data_out), .B_DATA_IN(registers_1_b_data_out), .OP_NOT(OPNOT), .OP_NAND(OPNAND),
    .CARRY_IN(F_CARRY), .OP_ADD(OPADD), .OP_SUB(OPSUB), .OP_SR(OPSR), .RESULT_OUT(RSO), .DATA_OUT(DATA_BUS),
    .CARRY_OUT(alu_1_carry_out[0]), .ZERO(alu_1_carry_out[1]), .SIGN(alu_1_carry_out[2]),
    .OVERFLOW(alu_1_carry_out[3]));
  Memory memory_1 (.CLK(CLK), .DATA_IN(DATA_BUS), .ADDR_IN(ADDRESS_BUS), .MI(MI), .MO(MO), .DATA_OUT(DATA_BUS));
  LED led_17 (.in(HLT));
  LED led_18 (.in(IEND));
  LED led_19 (.in(PCE));
  LED led_20 (.in(PCO));
  LED led_21 (.in(PCJ));
  LED led_22 (.in(AI));
  LED led_23 (.in(AO));
  LED led_24 (.in(BI));
  LED led_25 (.in(BO));
  LED led_26 (.in(RSO));
  LED led_27 (.in(OPADD));
  LED led_28 (.in(OPSUB));
  LED led_29 (.in(OPNOT));
  LED led_30 (.in(OPNAND));
  LED led_31 (.in(OPSR));
  LED led_32 (.in(FI));
  Pull_Resistor pull_resistor_1 (.node(DATA_BUS));
  Flags flags_1 (
    .CLK(CLK), .RESET(RESET), .DATA_IN(alu_1_carry_out), .ENABLE(FI),
    .DATA_OUT({flags_1_data_out, CONTROL_FLAGS}));
  assign DATA_BUS[3:0] = FO ? {flags_1_data_out, CONTROL_FLAGS} : 4'bz;  // Controlled_Buffer controlled_buffer_3
  Pull_Resistor pull_resistor_2 (.node(ADDRESS_BUS));

  // Notes on the sheet:
  //   Tower
endmodule

module ProgramCounter (
  input  CLK,
  input  RESET,
  input  J,
  input  CO,
  input  CE,
  input  [15:0] PC_ADDRESS_IN,
  output [15:0] PC_DATA_OUT
);

  wire counter_1_carry;
  wire [15:0] counter_1_q;

  Counter #(.max('hffff), .width(16)) counter_1 (
    .clr(RESET), .load(J), .up(1'b1), .count(CE), .clk(CLK), .D(PC_ADDRESS_IN), .carry(counter_1_carry),
    .Q(counter_1_q));
  Pull_Resistor pull_resistor_1 (.node(counter_1_carry));
  assign PC_DATA_OUT = CO ? counter_1_q : 16'bz;  // Controlled_Buffer controlled_buffer_1

  // Notes on the sheet:
  //   Program Counter
endmodule

module ALU (
  input  [7:0] A_DATA_IN,
  input  [7:0] B_DATA_IN,
  input  OP_NOT,
  input  OP_NAND,
  input  CARRY_IN,
  input  OP_ADD,
  input  OP_SUB,
  input  OP_SR,
  input  RESULT_OUT,
  output [7:0] DATA_OUT,
  output CARRY_OUT,
  output ZERO,
  output SIGN,
  output OVERFLOW
);

  wire adder_1_cout, and_1_out, and_2_out, or_1_out, or_2_out;
  wire [6:0] controlled_buffer_1_out;
  wire [7:0] adder_1_out, multiplexer_1_out, nand_1_out, not_1_out, not_2_out;

  // Probe on A_DATA_IN
  // Probe on B_DATA_IN
  or or_1 (or_1_out, OP_ADD, OP_SUB);
  assign not_1_out = ~A_DATA_IN;  // NOT_Gate not_1, 8 bits wide
  assign nand_1_out = ~(A_DATA_IN & B_DATA_IN);  // NAND_Gate nand_1, 8 bits wide
  or or_2 (or_2_out, CARRY_IN, OP_SUB);
  Multiplexer #(.width(8)) multiplexer_1 (.in0(B_DATA_IN), .in1(not_2_out), .out(multiplexer_1_out), .sel(OP_SUB));
  assign not_2_out = ~B_DATA_IN;  // NOT_Gate not_2, 8 bits wide
  Adder adder_1 (.a(A_DATA_IN), .b(multiplexer_1_out), .out(adder_1_out), .cin(or_2_out), .cout(adder_1_cout));
  assign {SIGN, controlled_buffer_1_out} = OP_SR ? {1'b0, A_DATA_IN[7:1]} : 8'bz;  // Controlled_Buffer controlled_buffer_1
  assign {SIGN, controlled_buffer_1_out} = OP_NOT ? not_1_out : 8'bz;  // Controlled_Buffer controlled_buffer_2
  Pull_Resistor pull_resistor_1 (.node({SIGN, controlled_buffer_1_out}));
  assign {SIGN, controlled_buffer_1_out} = OP_NAND ? nand_1_out : 8'bz;  // Controlled_Buffer controlled_buffer_3
  assign {SIGN, controlled_buffer_1_out} = or_1_out ? adder_1_out : 8'bz;  // Controlled_Buffer controlled_buffer_4
  and and_1 (and_1_out, or_1_out, adder_1_cout);
  or or_3 (CARRY_OUT, and_1_out, and_2_out);
  and and_2 (and_2_out, A_DATA_IN[0], OP_SR);
  nor nor_1 (ZERO, SIGN, controlled_buffer_1_out[6], controlled_buffer_1_out[5], controlled_buffer_1_out[4], controlled_buffer_1_out[3], controlled_buffer_1_out[2], controlled_buffer_1_out[1], controlled_buffer_1_out[0]);
  assign DATA_OUT = RESULT_OUT ? {SIGN, controlled_buffer_1_out} : 8'bz;  // Controlled_Buffer controlled_buffer_5
  // Probe on DATA_OUT

  assign OVERFLOW = 1'b0;

  // Notes on the sheet:
  //   ALU
endmodule

module Memory (
  input  CLK,
  input  [7:0] DATA_IN,
  input  [15:0] ADDR_IN,
  input  MI,
  input  MO,
  output [7:0] DATA_OUT
);

  wire and_1_out, or_1_out;
  wire [7:0] multiplexer_1_out, ram_1_dout, rom_1_data;

  ROM #(.addrWidth(16)) rom_1 (.addr(ADDR_IN), .data(rom_1_data));
  or or_1 (or_1_out, ADDR_IN[14], ADDR_IN[15]);
  and and_1 (and_1_out, or_1_out, MI);
  RAM #(.addrWidth(16)) ram_1 (.addr(ADDR_IN), .we(and_1_out), .oe(MO), .clk(CLK), .din(DATA_IN), .dout(ram_1_dout));
  Multiplexer #(.width(8)) multiplexer_1 (.in0(rom_1_data), .in1(ram_1_dout), .out(multiplexer_1_out), .sel(or_1_out));
  assign DATA_OUT = MO ? multiplexer_1_out : 8'bz;  // Controlled_Buffer controlled_buffer_1

  // Notes on the sheet:
  //   Memory
  //   contents of rom_1 (hex, n*v repeats v):
  //   f 11*0 f 8179*0 ff 53247*0 ff
endmodule

module Registers (
  input  CLK,
  input  RESET,
  input  [7:0] A_DATA_IN,
  input  AI,
  input  [7:0] B_DATA_IN,
  input  BI,
  output [7:0] A_DATA_OUT,
  output [7:0] B_DATA_OUT
);

  Register #(.trigger("falling")) A (.D(A_DATA_IN), .en(AI), .clk(CLK), .Q(A_DATA_OUT), .clr(RESET));
  Register #(.trigger("falling")) B (.D(B_DATA_IN), .en(BI), .clk(CLK), .Q(B_DATA_OUT), .clr(RESET));

  // Notes on the sheet:
  //   Registers
endmodule

module ControlLogic (
  input  CLK,
  input  RESET,
  input  [7:0] INSTRUCTION,
  input  [1:0] FLAGS,
  output [31:0] CONTROL_WORD
);

  wire [3:0] counter_1_q;

  Counter #(.max('hf), .width(4)) counter_1 (
    .clr(RESET), .load(1'b0), .up(1'b1), .clk(CLK), .Q(counter_1_q));  // open: count, D, carry
  ROM #(.addrWidth(14), .dataWidth(32)) rom_1 (.addr({counter_1_q, FLAGS, INSTRUCTION}), .data(CONTROL_WORD));

  // Notes on the sheet:
  //   Control logic
  //   Step counter
  //   Microcode
endmodule

module InstructionRegister (
  input  CLK,
  input  RESET,
  input  [7:0] DATA_IN,
  input  INI,
  output [7:0] DATA_OUT
);

  Register #(.trigger("falling")) register_1 (.D(DATA_IN), .en(INI), .clk(CLK), .Q(DATA_OUT), .clr(RESET));

  // Notes on the sheet:
  //   Instruction register
endmodule

module ArgumentRegisters (
  input  CLK,
  input  RESET,
  input  [7:0] DATA_IN,
  input  HI,
  input  LI,
  input  HO,
  input  LO,
  input  HLO,
  output [7:0] DATA_OUT,
  output [15:0] ADDRESS_OUT
);

  wire [7:0] H_q, L_q;

  Register #(.trigger("falling")) H (.D(DATA_IN), .en(HI), .clk(CLK), .Q(H_q), .clr(RESET));
  Register #(.trigger("falling")) L (.D(DATA_IN), .en(LI), .clk(CLK), .Q(L_q), .clr(RESET));
  assign DATA_OUT = HO ? H_q : 8'bz;  // Controlled_Buffer controlled_buffer_1
  assign DATA_OUT = LO ? L_q : 8'bz;  // Controlled_Buffer controlled_buffer_2
  assign ADDRESS_OUT = HLO ? {H_q, L_q} : 16'bz;  // Controlled_Buffer controlled_buffer_3

  // Notes on the sheet:
  //   Argument registers
endmodule

module Flags (
  input  CLK,
  input  RESET,
  input  [3:0] DATA_IN,
  input  ENABLE,
  output [3:0] DATA_OUT
);

  Register #(.trigger("falling"), .width(4)) F (.D(DATA_IN), .en(ENABLE), .clk(CLK), .Q(DATA_OUT), .clr(RESET));

  // Notes on the sheet:
  //   Flags
endmodule
